// Logisim project labo_checksum_etu.circ as structural Verilog: 9 circuits, main circuit Add1bit
module Add1bit (
  input  a_i,
  input  b_i,
  input  c_i,
  output r_o,
  output c_o
);

  wire and_1_out, and_2_out, and_3_out, xor_1_out;

  and and_1 (and_1_out, a_i, b_i);
  and and_2 (and_2_out, a_i, c_i);
  and and_3 (and_3_out, b_i, c_i);
  xor xor_1 (xor_1_out, a_i, b_i);
  xor xor_2 (r_o, xor_1_out, c_i);
  or or_1 (c_o, and_1_out, and_2_out, and_3_out);

  // Notes on the sheet:
  //   Attention, votre version de Logisim
  //   ne contient pas de tracker. Si vous
  //   enregistrez votre projet, toutes les
  //   informations du tracker seront
  //   définitivement effacées.
endmodule

module Add4bit (
  input  c_i,
  input  [3:0] a_i,
  input  [3:0] b_i,
  output [3:0] r_o,
  output c_o
);

  wire Add1Bit_1_c_o, Add1Bit_2_c_o, Add1Bit_3_c_o;

  Add1bit Add1Bit_1 (.a_i(a_i[0]), .b_i(b_i[0]), .c_i(c_i), .r_o(r_o[0]), .c_o(Add1Bit_1_c_o));
  Add1bit Add1Bit_2 (.a_i(a_i[1]), .b_i(b_i[1]), .c_i(Add1Bit_1_c_o), .r_o(r_o[1]), .c_o(Add1Bit_2_c_o));
  Add1bit Add1Bit_3 (.a_i(a_i[2]), .b_i(b_i[2]), .c_i(Add1Bit_2_c_o), .r_o(r_o[2]), .c_o(Add1Bit_3_c_o));
  Add1bit Add1Bit_4 (.a_i(a_i[3]), .b_i(b_i[3]), .c_i(Add1Bit_3_c_o), .r_o(r_o[3]), .c_o(c_o));

  // Notes on the sheet:
  //   Attention, votre version de Logisim
  //   ne contient pas de tracker. Si vous
  //   enregistrez votre projet, toutes les
  //   informations du tracker seront
  //   définitivement effacées.
endmodule

module Sub4bit (
  input  [3:0] a_i,
  input  [3:0] b_i,
  output [3:0] r_o,
  output c_o
);

  wire [3:0] not_1_out;

  assign not_1_out = ~b_i;  // NOT_Gate not_1, 4 bits wide
  Add4bit Add4Bit_1 (.c_i(1'b1), .a_i(a_i), .b_i(not_1_out), .r_o(r_o), .c_o(c_o));

  // Notes on the sheet:
  //   Attention, votre version de Logisim
  //   ne contient pas de tracker. Si vous
  //   enregistrez votre projet, toutes les
  //   informations du tracker seront
  //   définitivement effacées.
endmodule

module AddSub4bit (
  input  sel_i,
  input  [3:0] a_i,
  input  [3:0] b_i,
  output [3:0] r_o,
  output c_o
);

  wire [3:0] xor_1_out;

  assign xor_1_out = b_i ^ {4{sel_i}};  // XOR_Gate xor_1, 4 bits wide
  Add4bit Add1Bit_1 (.c_i(sel_i), .a_i(a_i), .b_i(xor_1_out), .r_o(r_o), .c_o(c_o));

  // Notes on the sheet:
  //   Attention, votre version de Logisim
  //   ne contient pas de tracker. Si vous
  //   enregistrez votre projet, toutes les
  //   informations du tracker seront
  //   définitivement effacées.
endmodule

module Add8bit (
  input  c_i,
  input  [7:0] a_i,
  input  [7:0] b_i,
  output [7:0] r_o,
  output c_o
);

  wire Add4Bit_1_c_o;

  Add4bit Add4Bit_1 (.c_i(c_i), .a_i(a_i[3:0]), .b_i(b_i[3:0]), .r_o(r_o[3:0]), .c_o(Add4Bit_1_c_o));
  Add4bit Add4Bit_2 (.c_i(Add4Bit_1_c_o), .a_i(a_i[7:4]), .b_i(b_i[7:4]), .r_o(r_o[7:4]), .c_o(c_o));

  // Notes on the sheet:
  //   Attention, votre version de Logisim
  //   ne contient pas de tracker. Si vous
  //   enregistrez votre projet, toutes les
  //   informations du tracker seront
  //   définitivement effacées.
endmodule

module AddSub8bit (
  input  sel_i,
  input  [7:0] a_i,
  input  [7:0] b_i,
  output [7:0] r_o,
  output c_o
);

  wire [7:0] xor_1_out;

  assign xor_1_out = b_i ^ {8{sel_i}};  // XOR_Gate xor_1, 8 bits wide
  Add8bit Add8Bit_1 (.c_i(sel_i), .a_i(a_i), .b_i(xor_1_out), .r_o(r_o), .c_o(c_o));

  // Notes on the sheet:
  //   Attention, votre version de Logisim
  //   ne contient pas de tracker. Si vous
  //   enregistrez votre projet, toutes les
  //   informations du tracker seront
  //   définitivement effacées.
endmodule

module Checksum (
  input  [7:0] a_i,
  input  [7:0] b_i,
  input  [7:0] c_i,
  output [7:0] r_o
);

  wire [7:0] AddSub8Bit_1_r_o, AddSub8Bit_2_r_o, not_1_out;

  AddSub8bit AddSub8Bit_1 (.sel_i(1'b0), .a_i(a_i), .b_i(b_i), .r_o(AddSub8Bit_1_r_o));  // open: c_o
  AddSub8bit AddSub8Bit_2 (.sel_i(1'b0), .a_i(AddSub8Bit_1_r_o), .b_i(c_i), .r_o(AddSub8Bit_2_r_o));  // open: c_o
  assign not_1_out = ~AddSub8Bit_2_r_o;  // NOT_Gate not_1, 8 bits wide
  AddSub8bit AddSub8Bit_3 (.sel_i(1'b0), .a_i(8'h1), .b_i(not_1_out), .r_o(r_o));  // open: c_o

  // Notes on the sheet:
  //   Attention, votre version de Logisim
  //   ne contient pas de tracker. Si vous
  //   enregistrez votre projet, toutes les
  //   informations du tracker seront
  //   définitivement effacées.
endmodule

module VerifyIntegrity (
  input  [7:0] a_i,
  input  [7:0] b_i,
  input  [7:0] c_i,
  input  [7:0] d_i,
  output verif_checksum_o
);

  wire [7:0] Add8Bit_1_r_o, Add8Bit_2_r_o, Add8Bit_3_r_o;

  Add8bit Add8Bit_1 (.c_i(1'b0), .a_i(a_i), .b_i(b_i), .r_o(Add8Bit_1_r_o));  // open: c_o
  Add8bit Add8Bit_2 (.c_i(1'b0), .a_i(c_i), .b_i(d_i), .r_o(Add8Bit_2_r_o));  // open: c_o
  Add8bit Add8Bit_3 (.c_i(1'b0), .a_i(Add8Bit_1_r_o), .b_i(Add8Bit_2_r_o), .r_o(Add8Bit_3_r_o));  // open: c_o
  nor nor_1 (verif_checksum_o, Add8Bit_3_r_o[0], Add8Bit_3_r_o[1], Add8Bit_3_r_o[2], Add8Bit_3_r_o[3], Add8Bit_3_r_o[4], Add8Bit_3_r_o[5], Add8Bit_3_r_o[6], Add8Bit_3_r_o[7]);

  // Notes on the sheet:
  //   Attention, votre version de Logisim
  //   ne contient pas de tracker. Si vous
  //   enregistrez votre projet, toutes les
  //   informations du tracker seront
  //   définitivement effacées.
endmodule

module main (
);

  wire [7:0] Btn_1_out, checksum_1_r_o;

  Button Btn_2 (.out(Btn_1_out[1]));
  Button Btn_4 (.out(Btn_1_out[3]));
  Button Btn_6 (.out(Btn_1_out[5]));
  Button Btn_8 (.out(Btn_1_out[7]));
  Button Btn_1 (.out(Btn_1_out[0]));
  Button Btn_3 (.out(Btn_1_out[2]));
  Button Btn_5 (.out(Btn_1_out[4]));
  Button Btn_7 (.out(Btn_1_out[6]));
  LED Led_1 (.in(checksum_1_r_o[0]));
  LED Led_2 (.in(checksum_1_r_o[1]));
  LED Led_3 (.in(checksum_1_r_o[2]));
  Checksum checksum_1 (.a_i({8{1'b0}}), .b_i({8{1'b0}}), .c_i(Btn_1_out), .r_o(checksum_1_r_o));
  LED Led_4 (.in(checksum_1_r_o[3]));
  LED Led_5 (.in(checksum_1_r_o[4]));
  LED Led_6 (.in(checksum_1_r_o[5]));
  LED Led_7 (.in(checksum_1_r_o[6]));
  LED Led_8 (.in(checksum_1_r_o[7]));

  // Notes on the sheet:
  //   Attention, votre version de Logisim
  //   ne contient pas de tracker. Si vous
  //   enregistrez votre projet, toutes les
  //   informations du tracker seront
  //   définitivement effacées.
endmodule
