// Logisim project labo_alu_etu.circ as structural Verilog: 11 circuits, main circuit ALU_MAXV
module ALU_MAXV (
  input  [3:0] a_i,
  input  [3:0] b_i,
  output erreur_o,
  output [3:0] c_o
);

  wire [5:0] opcode_i_sw6;

  DipSwitch opcode_i (
    .sw1(opcode_i_sw6[5]), .sw2(opcode_i_sw6[4]), .sw3(opcode_i_sw6[3]), .sw4(opcode_i_sw6[2]),
    .sw5(opcode_i_sw6[1]), .sw6(opcode_i_sw6[0]));  // open: sw7, sw8
  ALU_Top alu_inst (.a_i(a_i), .b_i(b_i), .op_i(opcode_i_sw6), .erreur_o(erreur_o), .c_o(c_o));

  // Notes on the sheet:
  //   Attention, votre version de Logisim
  //   ne contient pas de tracker. Si vous
  //   enregistrez votre projet, toutes les
  //   informations du tracker seront
  //   définitivement effacées.
endmodule

module ALU_Top (
  input  [3:0] a_i,
  input  [3:0] b_i,
  input  [5:0] op_i,
  output erreur_o,
  output [3:0] c_o
);

  wire addsub_1_carry_o, addsub_1_overflow_o, addsub_1_r_o_3, addsub_1_zero_o;
  wire [3:0] addsub_o, cmp_o, custom_o, logique_o;

  Logique logique_1 (.a_i(a_i), .b_i(b_i), .op_i(op_i[1:0]), .f_o(logique_o));
  Custom custom_1 (.a_i(a_i), .s_o(custom_o));
  AddSub addsub_1 (
    .op_i(op_i[3:2]), .a_i(a_i), .b_i(b_i), .r_o(addsub_o), .zero_o(addsub_1_zero_o), .r_o_3(addsub_1_r_o_3),
    .carry_o(addsub_1_carry_o), .overflow_o(addsub_1_overflow_o));
  Comparateur comparateur_1 (
    .a_i_3(a_i[3]), .b_i_3(b_i[3]), .r_i_3(addsub_1_r_o_3), .zero_i(addsub_1_zero_o),
    .carry_i(addsub_1_carry_o), .op_i(op_i[2:0]), .cmp_o(cmp_o));
  Multiplexer #(.select(2), .width(4), .enable("false")) multiplexer_1 (
    .in0(addsub_o), .in1(cmp_o), .in2(logique_o), .in3(custom_o), .out(c_o), .sel(op_i[5:4]));
  Erreur erreur_1 (.op_i(op_i), .overflow_i(addsub_1_overflow_o), .erreur_o(erreur_o));

  // Other names for the same wires on the sheet: opcode_addsub[1:0] = op_i[3:2]; opcode_total[5:0] = op_i;
  //   opcode_comparateur[2:0] = op_i[2:0]; opcode_fonctionnalite[1:0] = op_i[5:4]; opcode_logique[1:0] = op_i[1:0]

  // Notes on the sheet:
  //   Attention, votre version de Logisim
  //   ne contient pas de tracker. Si vous
  //   enregistrez votre projet, toutes les
  //   informations du tracker seront
  //   définitivement effacées.
endmodule

module Add1bit (
  input  a_i,
  input  b_i,
  input  c_i,
  output r_o,
  output c_o
);

  wire and_1_out, and_2_out, and_3_out, xor_1_out;

  and and_1 (and_1_out, a_i, b_i);
  and and_2 (and_2_out, a_i, c_i);
  and and_3 (and_3_out, b_i, c_i);
  xor xor_1 (xor_1_out, a_i, b_i);
  xor xor_2 (r_o, xor_1_out, c_i);
  or or_1 (c_o, and_1_out, and_2_out, and_3_out);

  // Notes on the sheet:
  //   Attention, votre version de Logisim
  //   ne contient pas de tracker. Si vous
  //   enregistrez votre projet, toutes les
  //   informations du tracker seront
  //   définitivement effacées.
endmodule

module Add4bit (
  input  c_i,
  input  [3:0] a_i,
  input  [3:0] b_i,
  output [3:0] r_o,
  output c_o
);

  wire Add1Bit_1_c_o, Add1Bit_2_c_o, Add1Bit_3_c_o;

  Add1bit Add1Bit_1 (.a_i(a_i[0]), .b_i(b_i[0]), .c_i(c_i), .r_o(r_o[0]), .c_o(Add1Bit_1_c_o));
  Add1bit Add1Bit_2 (.a_i(a_i[1]), .b_i(b_i[1]), .c_i(Add1Bit_1_c_o), .r_o(r_o[1]), .c_o(Add1Bit_2_c_o));
  Add1bit Add1Bit_3 (.a_i(a_i[2]), .b_i(b_i[2]), .c_i(Add1Bit_2_c_o), .r_o(r_o[2]), .c_o(Add1Bit_3_c_o));
  Add1bit Add1Bit_4 (.a_i(a_i[3]), .b_i(b_i[3]), .c_i(Add1Bit_3_c_o), .r_o(r_o[3]), .c_o(c_o));

  // Notes on the sheet:
  //   Attention, votre version de Logisim
  //   ne contient pas de tracker. Si vous
  //   enregistrez votre projet, toutes les
  //   informations du tracker seront
  //   définitivement effacées.
endmodule

module AddSub (
  input  [1:0] op_i,
  input  [3:0] a_i,
  input  [3:0] b_i,
  output [3:0] r_o,
  output zero_o,
  output r_o_3,
  output carry_o,
  output overflow_o
);

  AddSub4bit addsub4bit_1 (.sel_i(op_i[1]), .a_i(a_i), .b_i(b_i), .r_o(r_o), .c_o(carry_o));
  nor nor_1 (zero_o, r_o[0], r_o[1], r_o[2], r_o[3]);
  Overflow overflow_1 (
    .a_3(a_i[3]), .b_3(b_i[3]), .r_3(r_o[3]), .carry_i(carry_o), .op_i(op_i), .overflow_o(overflow_o));

  assign r_o_3 = r_o[3];

  // Notes on the sheet:
  //   Attention, votre version de Logisim
  //   ne contient pas de tracker. Si vous
  //   enregistrez votre projet, toutes les
  //   informations du tracker seront
  //   définitivement effacées.
endmodule

module AddSub4bit (
  input  sel_i,
  input  [3:0] a_i,
  input  [3:0] b_i,
  output [3:0] r_o,
  output c_o
);

  wire [3:0] xor_1_out;

  assign xor_1_out = b_i ^ {4{sel_i}};  // XOR_Gate xor_1, 4 bits wide
  Add4bit add4bit_1 (.c_i(sel_i), .a_i(a_i), .b_i(xor_1_out), .r_o(r_o), .c_o(c_o));

  // Notes on the sheet:
  //   Attention, votre version de Logisim
  //   ne contient pas de tracker. Si vous
  //   enregistrez votre projet, toutes les
  //   informations du tracker seront
  //   définitivement effacées.
endmodule

module Comparateur (
  input  a_i_3,
  input  b_i_3,
  input  r_i_3,
  input  zero_i,
  input  carry_i,
  input  [2:0] op_i,
  output [3:0] cmp_o
);

  wire and_1_out, and_2_out, and_3_out, and_4_out, not_1_out, not_2_out, or_1_out, or_2_out, xnor_1_out,
       xnor_2_out;

  and and_1 (and_1_out, ~a_i_3, b_i_3);  // AND_Gate
  and and_2 (and_2_out, ~r_i_3, xnor_1_out);  // AND_Gate
  xnor xnor_1 (xnor_1_out, a_i_3, b_i_3);
  and and_3 (and_3_out, a_i_3, ~b_i_3);  // AND_Gate
  and and_4 (and_4_out, r_i_3, xnor_2_out);
  xnor xnor_2 (xnor_2_out, a_i_3, b_i_3);
  or or_1 (or_1_out, and_1_out, and_2_out);
  or or_2 (or_2_out, and_3_out, and_4_out);
  not not_1 (not_1_out, zero_i);
  not not_2 (not_2_out, carry_i);
  Multiplexer #(.select(3), .enable("false")) multiplexer_1 (
    .in0(1'b0), .in1(or_1_out), .in2(or_2_out), .in3(not_1_out), .in4(zero_i), .in5(carry_i),
    .in6(not_2_out), .in7(1'b0), .out(cmp_o[0]), .sel(op_i));

  assign cmp_o[3:1] = 3'b000;

  // Notes on the sheet:
  //   Attention, votre version de Logisim
  //   ne contient pas de tracker. Si vous
  //   enregistrez votre projet, toutes les
  //   informations du tracker seront
  //   définitivement effacées.
endmodule

module Logique (
  input  [3:0] a_i,
  input  [3:0] b_i,
  input  [1:0] op_i,
  output [3:0] f_o
);

  wire [3:0] and_1_out, nand_1_out, or_1_out, xor_1_out;

  assign and_1_out = a_i & b_i;  // AND_Gate and_1, 4 bits wide
  assign or_1_out = a_i | b_i;  // OR_Gate or_1, 4 bits wide
  assign nand_1_out = ~(a_i & b_i);  // NAND_Gate nand_1, 4 bits wide
  assign xor_1_out = a_i ^ b_i;  // XOR_Gate xor_1, 4 bits wide
  Multiplexer #(.select(2), .width(4), .enable("false")) multiplexer_1 (
    .in0(and_1_out), .in1(or_1_out), .in2(nand_1_out), .in3(xor_1_out), .out(f_o), .sel(op_i));

  // Notes on the sheet:
  //   Attention, votre version de Logisim
  //   ne contient pas de tracker. Si vous
  //   enregistrez votre projet, toutes les
  //   informations du tracker seront
  //   définitivement effacées.
endmodule

module Custom (
  input  [3:0] a_i,
  output [3:0] s_o
);

  wire add1bit_1_c_o, add1bit_1_r_o, add1bit_2_c_o, add1bit_2_r_o, add1bit_3_c_o;

  Add1bit add1bit_1 (.a_i(a_i[0]), .b_i(a_i[1]), .c_i(1'b0), .r_o(add1bit_1_r_o), .c_o(add1bit_1_c_o));
  Add1bit add1bit_2 (.a_i(a_i[2]), .b_i(a_i[3]), .c_i(1'b0), .r_o(add1bit_2_r_o), .c_o(add1bit_2_c_o));
  Add1bit add1bit_3 (.a_i(add1bit_1_r_o), .b_i(add1bit_2_r_o), .c_i(1'b0), .r_o(s_o[0]), .c_o(add1bit_3_c_o));
  Add1bit add1bit_4 (.a_i(add1bit_1_c_o), .b_i(add1bit_2_c_o), .c_i(add1bit_3_c_o), .r_o(s_o[1]), .c_o(s_o[2]));

  assign s_o[3] = 1'b0;

  // Notes on the sheet:
  //   Attention, votre version de Logisim
  //   ne contient pas de tracker. Si vous
  //   enregistrez votre projet, toutes les
  //   informations du tracker seront
  //   définitivement effacées.
endmodule

module Overflow (
  input  a_3,
  input  b_3,
  input  r_3,
  input  carry_i,
  input  [1:0] op_i,
  output overflow_o
);

  wire and_1_out, and_2_out, and_3_out, and_4_out, multiplexer_1_out, multiplexer_3_out, not_1_out, or_1_out,
       or_2_out;

  and and_1 (and_1_out, ~a_3, ~b_3, r_3);  // AND_Gate
  and and_2 (and_2_out, a_3, b_3, ~r_3);  // AND_Gate
  and and_3 (and_3_out, ~a_3, b_3, r_3);  // AND_Gate
  and and_4 (and_4_out, a_3, ~b_3, ~r_3);  // AND_Gate
  or or_1 (or_1_out, and_1_out, and_2_out);
  Multiplexer #(.enable("false")) multiplexer_1 (
    .in0(or_1_out), .in1(or_2_out), .out(multiplexer_1_out), .sel(op_i[1]));
  or or_2 (or_2_out, and_3_out, and_4_out);
  not not_1 (not_1_out, carry_i);
  Multiplexer #(.enable("false")) multiplexer_2 (
    .in0(multiplexer_1_out), .in1(multiplexer_3_out), .out(overflow_o), .sel(op_i[0]));
  Multiplexer #(.enable("false")) multiplexer_3 (
    .in0(carry_i), .in1(not_1_out), .out(multiplexer_3_out), .sel(op_i[1]));

  // Notes on the sheet:
  //   Attention, votre version de Logisim
  //   ne contient pas de tracker. Si vous
  //   enregistrez votre projet, toutes les
  //   informations du tracker seront
  //   définitivement effacées.
endmodule

module Erreur (
  input  [5:0] op_i,
  input  overflow_i,
  output erreur_o
);

  wire and_1_out, and_2_out, and_3_out, and_4_out;

  and and_1 (and_1_out, ~op_i[5], op_i[4], ~op_i[3]);  // AND_Gate
  and and_2 (and_2_out, ~op_i[5], op_i[4], op_i[3], op_i[2], op_i[1], op_i[0]);  // AND_Gate
  and and_3 (and_3_out, ~op_i[5], op_i[4], op_i[3], ~op_i[2], ~op_i[1], ~op_i[0]);  // AND_Gate
  and and_4 (and_4_out, ~op_i[5], ~op_i[4], overflow_i);  // AND_Gate
  or or_1 (erreur_o, and_1_out, and_2_out, and_3_out, and_4_out);

  // Notes on the sheet:
  //   Attention, votre version de Logisim
  //   ne contient pas de tracker. Si vous
  //   enregistrez votre projet, toutes les
  //   informations du tracker seront
  //   définitivement effacées.
endmodule
