// Logisim project labo_uart_etu.circ as structural Verilog: 6 circuits, main circuit MAXV_UART
module MAXV_UART (
  input  [7:0] switch_i,
  input  send_i,
  input  clk_i,
  input  nReset_i,
  output [1:0] conf_MAX10_o,
  output TX_done_o
);

  wire not_1_out;
  wire [3:0] Leds_select_i_sw1;
  wire [29:29] tx_uart_serial_tx_o;

  DipSwitch Leds_select_i (
    .sw1(Leds_select_i_sw1[0]), .sw2(Leds_select_i_sw1[1]), .sw3(Leds_select_i_sw1[2]),
    .sw4(Leds_select_i_sw1[3]));  // open: sw5, sw6, sw7, sw8
  not not_1 (not_1_out, nReset_i);
  uart_tx tx_uart (
    .data_i({Leds_select_i_sw1, 8'h55, switch_i}), .clk_i(clk_i), .reset_i(not_1_out), .send_i(send_i),
    .serial_tx_o(tx_uart_serial_tx_o[29]), .tx_done_o(TX_done_o));
  // PortIO #(.number(78)) Con_80p_io: pin names not known; wires that end beside it: {2'b00, tx_uart_serial_tx_o[29], {29{1'b0}}}, {32{1'b0}}, {6'b010000, conf_MAX10_o, {6{1'b0}}}

  // Notes on the sheet:
  //   Attention, votre version de Logisim
  //   ne contient pas de tracker. Si vous
  //   enregistrez votre projet, toutes les
  //   informations du tracker seront
  //   définitivement effacées.
  //   Configuration MAX10 en mode UART
  //   0 = Config non-reconnue
  //   1 = Config connue
  //   Sortie de la config de la MAX10 sur 2 LEDs.
endmodule

module uart_tx (
  input  [19:0] data_i,
  input  clk_i,
  input  reset_i,
  input  send_i,
  output serial_tx_o,
  output tx_done_o
);

  wire or_1_out, reset_i_t, timer_12b_2_done_o;
  wire [1:0] mode_o;
  wire [23:0] data_i_t;

  or or_1 (or_1_out, mode_o[0], timer_12b_2_done_o);
  timer_12b timer_12b_2 (
    .value_i(12'hc34), .clk_i(clk_i), .reset_i(reset_i_t), .load_i(or_1_out), .en_i(1'b1),
    .done_o(timer_12b_2_done_o));
  shift_reg_24b shift_reg_24b_1 (
    .ser_r_i(1'b0), .value_load_i({1'b0, data_i, 3'b111}), .mode_i(mode_o), .clk_i(clk_i),
    .reset_i(reset_i_t), .ser_l_i(1'b0), .val_o(data_i_t));
  controle controle_1 (
    .send_i(send_i), .clk_i(clk_i), .reset_i(reset_i), .data_i(data_i_t), .timer_done_i(timer_12b_2_done_o),
    .reset_o(reset_i_t), .mode_o(mode_o), .tx_done_o(tx_done_o));
  Multiplexer #(.enable("false")) multiplexer_1 (.in0(data_i_t[23]), .in1(1'b1), .out(serial_tx_o), .sel(tx_done_o));

  // Notes on the sheet:
  //   Attention, votre version de Logisim
  //   ne contient pas de tracker. Si vous
  //   enregistrez votre projet, toutes les
  //   informations du tracker seront
  //   définitivement effacées.
endmodule

module shift_reg_4b (
  input  ser_l_i,
  input  [3:0] value_load_i,
  input  [1:0] mode_i,
  input  ser_r_i,
  input  clk_i,
  input  reset_i,
  output [3:0] val_o
);

  wire multiplexer_1_out, multiplexer_2_out, multiplexer_3_out, multiplexer_4_out;

  Multiplexer #(.select(2), .enable("false")) multiplexer_1 (
    .in0(val_o[3]), .in1(value_load_i[3]), .in2(val_o[2]), .in3(ser_r_i), .out(multiplexer_1_out),
    .sel(mode_i));
  D_Flip_Flop flipflopD_1 (
    .D(multiplexer_1_out), .clk(clk_i), .Q(val_o[3]), .preset(1'b0), .reset(reset_i));  // open: Qn
  Multiplexer #(.select(2), .enable("false")) multiplexer_2 (
    .in0(val_o[2]), .in1(value_load_i[2]), .in2(val_o[1]), .in3(val_o[3]), .out(multiplexer_2_out),
    .sel(mode_i));
  D_Flip_Flop flipflopD_2 (
    .D(multiplexer_2_out), .clk(clk_i), .Q(val_o[2]), .preset(1'b0), .reset(reset_i));  // open: Qn
  Multiplexer #(.select(2), .enable("false")) multiplexer_3 (
    .in0(val_o[1]), .in1(value_load_i[1]), .in2(val_o[0]), .in3(val_o[2]), .out(multiplexer_3_out),
    .sel(mode_i));
  D_Flip_Flop flipflopD_3 (
    .D(multiplexer_3_out), .clk(clk_i), .Q(val_o[1]), .preset(1'b0), .reset(reset_i));  // open: Qn
  Multiplexer #(.select(2), .enable("false")) multiplexer_4 (
    .in0(val_o[0]), .in1(value_load_i[0]), .in2(ser_l_i), .in3(val_o[1]), .out(multiplexer_4_out),
    .sel(mode_i));
  D_Flip_Flop flipflopD_4 (
    .D(multiplexer_4_out), .clk(clk_i), .Q(val_o[0]), .preset(1'b0), .reset(reset_i));  // open: Qn

  // Notes on the sheet:
  //   Attention, votre version de Logisim
  //   ne contient pas de tracker. Si vous
  //   enregistrez votre projet, toutes les
  //   informations du tracker seront
  //   définitivement effacées.
endmodule

module shift_reg_24b (
  input  ser_r_i,
  input  [23:0] value_load_i,
  input  [1:0] mode_i,
  input  clk_i,
  input  reset_i,
  input  ser_l_i,
  output [23:0] val_o
);

  shift_reg_4b shift_reg_4b_1 (
    .ser_l_i(val_o[19]), .value_load_i(value_load_i[23:20]), .mode_i(mode_i), .ser_r_i(ser_r_i),
    .clk_i(clk_i), .reset_i(reset_i), .val_o(val_o[23:20]));
  shift_reg_4b shift_reg_4b_2 (
    .ser_l_i(val_o[15]), .value_load_i(value_load_i[19:16]), .mode_i(mode_i), .ser_r_i(val_o[20]),
    .clk_i(clk_i), .reset_i(reset_i), .val_o(val_o[19:16]));
  shift_reg_4b shift_reg_4b_3 (
    .ser_l_i(val_o[11]), .value_load_i(value_load_i[15:12]), .mode_i(mode_i), .ser_r_i(val_o[16]),
    .clk_i(clk_i), .reset_i(reset_i), .val_o(val_o[15:12]));
  shift_reg_4b shift_reg_4b_4 (
    .ser_l_i(val_o[7]), .value_load_i(value_load_i[11:8]), .mode_i(mode_i), .ser_r_i(val_o[12]),
    .clk_i(clk_i), .reset_i(reset_i), .val_o(val_o[11:8]));
  shift_reg_4b shift_reg_4b_5 (
    .ser_l_i(val_o[3]), .value_load_i(value_load_i[7:4]), .mode_i(mode_i), .ser_r_i(val_o[8]), .clk_i(clk_i),
    .reset_i(reset_i), .val_o(val_o[7:4]));
  shift_reg_4b shift_reg_4b_6 (
    .ser_l_i(ser_l_i), .value_load_i(value_load_i[3:0]), .mode_i(mode_i), .ser_r_i(val_o[4]), .clk_i(clk_i),
    .reset_i(reset_i), .val_o(val_o[3:0]));

  // Notes on the sheet:
  //   Attention, votre version de Logisim
  //   ne contient pas de tracker. Si vous
  //   enregistrez votre projet, toutes les
  //   informations du tracker seront
  //   définitivement effacées.
endmodule

module timer_12b (
  input  [11:0] value_i,
  input  clk_i,
  input  reset_i,
  input  load_i,
  input  en_i,
  output done_o
);

  wire and_1_out, and_2_out, or_1_out;
  wire [11:0] multiplexer_1_out, reg_0_q, subtractor_1_out;

  Subtractor #(.width(12)) subtractor_1 (.a(reg_0_q), .b(12'h1), .out(subtractor_1_out));  // open: bin, bout
  Multiplexer #(.width(12), .enable("false")) multiplexer_1 (
    .in0(subtractor_1_out), .in1(value_i), .out(multiplexer_1_out), .sel(load_i));
  and and_1 (and_1_out, load_i, en_i);
  and and_2 (and_2_out, en_i, ~done_o);  // AND_Gate
  or or_1 (or_1_out, and_1_out, and_2_out);
  Register #(.width(12)) reg_0 (.D(multiplexer_1_out), .en(or_1_out), .clk(clk_i), .Q(reg_0_q), .clr(reset_i));
  Comparator #(.width(12)) comparator_1 (.a(reg_0_q), .b({12{1'b0}}), .eq(done_o));  // open: gt, lt

  // Notes on the sheet:
  //   Attention, votre version de Logisim
  //   ne contient pas de tracker. Si vous
  //   enregistrez votre projet, toutes les
  //   informations du tracker seront
  //   définitivement effacées.
endmodule

module controle (
  input  send_i,
  input  clk_i,
  input  reset_i,
  input  [23:0] data_i,
  input  timer_done_i,
  output reset_o,
  output [1:0] mode_o,
  output tx_done_o
);

  wire and_1_out, comparator_1_eq, comparator_2_eq, d_ff_1_q, d_ff_2_qn, lock_o, mode_o_t;

  D_Flip_Flop d_ff_1 (.D(send_i), .clk(clk_i), .Q(d_ff_1_q), .preset(1'b0), .reset(reset_i));  // open: Qn
  D_Flip_Flop d_ff_2 (.D(d_ff_1_q), .clk(clk_i), .Qn(d_ff_2_qn), .preset(1'b0), .reset(reset_i));  // open: Q
  Comparator #(.width(24)) comparator_1 (.a(data_i), .b(24'h800000), .eq(comparator_1_eq));  // open: gt, lt
  Comparator #(.width(24)) comparator_2 (.a(data_i), .b({24{1'b0}}), .eq(comparator_2_eq));  // open: gt, lt
  D_Flip_Flop d_ff_3 (.D(and_1_out), .clk(clk_i), .Q(mode_o[0]), .preset(1'b0), .reset(reset_i));  // open: Qn
  or or_1 (tx_done_o, comparator_1_eq, comparator_2_eq);
  and and_1 (and_1_out, d_ff_1_q, d_ff_2_qn);
  D_Flip_Flop d_ff_4 (.D(mode_o[0]), .clk(clk_i), .Q(mode_o_t), .preset(lock_o), .reset(reset_i));  // open: Qn
  or or_2 (reset_o, and_1_out, reset_i);
  and and_2 (mode_o[1], mode_o_t, timer_done_i);
  and and_3 (lock_o, mode_o_t, ~tx_done_o);  // AND_Gate

  // Notes on the sheet:
  //   Attention, votre version de Logisim
  //   ne contient pas de tracker. Si vous
  //   enregistrez votre projet, toutes les
  //   informations du tracker seront
  //   définitivement effacées.
  //   Gestion du flanc montant
  //   Détecte on est au bit de stop
  //   Actif si pas de transmission (0)
  //   Active le mode 01 (LOAD)
  //   Active SHL (10)
  //   Autorise le SHL
  //   Vérouille l'état d'envoi, tant que c'est pas done
  //   Etat de reset qui s'active avant qu'on send et lorsque on reset
endmodule
